# Fritzing sketch Receiver (saved by Fritzing 0.9.3b)
circuit board: 10cm x 6cm

parts:
  Part1 = Arduino Nano (Rev3.0)
  HC-1 = HC-12 Module
  Antenna1 = HC-12 Antenna
  U1 = LIPO-1000mAh [part_number=7.4V package=lipo-1000]
  J1 = Basic Servo
  J2 = Basic Servo
  U2 = RELAY [package=relay-jzc]
  U3 = RELAY [package=relay-jzc]
  U4 = RELAY [package=relay-jzc]
  U5 = RELAY [package=relay-jzc]
  U6 = RELAY [package=relay-jzc]
  U7 = RELAY [package=relay-jzc]
  U8 = RELAY [package=relay-jzc]
  U9 = RELAY [package=relay-jzc]

nets:
  N1: Part1.D2, HC-1.RXD
  N2: Part1.D3, HC-1.TXD
  N3: Part1.D4, U2.NO
  N4: Part1.D5, U3.NO
  N5: Part1.D6, U4.NO
  N6: Part1.D7, U5.NO
  N7: Part1.D8, U9.NO
  N8: Part1.D9, U8.NO
  N9: Part1.D10, J1.pulse
  N10: Part1.D11/MOSI, J2.pulse
  N11: Part1.D12/MISO, U7.NO
  GND: Part1.GND, HC-1.GND, U1.-, J1.gnd, J2.gnd
  N12: Part1.D13/SCK, U6.NO
  N13: HC-1.VCC, U1.+
  N14: HC-1.ANT, Antenna1.ANT
  VCC: J1.vcc, J2.vcc
  N15: U2.COIL2, U3.COIL2
  N16: U6.COIL2, U7.COIL2
  N17: U8.NC, U9.NC

custom parts:
  HC-12 Module: HC-12 433Mhz Module
  HC-12 Antenna: Antenna for HC-12 433Mhz Module
