# Fritzing sketch Sender (saved by Fritzing 0.9.3b)

parts:
  Part1 = Arduino Nano (Rev3.0)
  HC-1 = HC-12 Module
  Antenna1 = HC-12 Antenna  # not connected
  R1 = Resistor [tolerance=±5% resistance=220 package=THT]
  Key1 = Pushbutton [package="[SMD]"]
  Key2 = Pushbutton [package="[SMD]"]
  Key3 = Pushbutton [package="[THT]"]
  Key4 = Pushbutton [package="[THT]"]
  Key5 = Pushbutton [package="[THT]"]
  Key6 = Pushbutton [package="[THT]"]
  Key7 = Pushbutton [package="[THT]"]
  R2 = Resistor [tolerance=±5% resistance=330 package=THT]
  R3 = Resistor [tolerance=±5% resistance=470 package=THT]
  R4 = Resistor [tolerance=±5% resistance=680 package=THT]
  R5 = Resistor [tolerance=±5% resistance=1k package=THT]
  R6 = Resistor [tolerance=±5% resistance=1.5k package=THT]
  R7 = Resistor [tolerance=±5% resistance=2.2k package=THT]
  Trim3 = Rotary Potentiometer (Large) [maximum_resistance=100kΩ package=THT]
  Trim2 = Rotary Potentiometer (Large) [maximum_resistance=100kΩ package=THT]
  Trim3_2 = Rotary Potentiometer (Large) [maximum_resistance=100kΩ package=THT]
  Key1_LED = LED - 3mm [color="Red (635nm)" package="3 mm [THT]"]
  Key2_LED = LED - 3mm [color="Red (633nm)" package="3 mm [THT]"]
  R9 = Resistor [tolerance=±5% resistance=5.1m package=THT]
  R10 = Resistor [tolerance=±5% resistance=10m package="0603 [SMD]"]
  C1 = Ceramic Capacitor [capacitance="100 nF" package="0805 [SMD, multilayer]"]  # not connected
  Grove1 = Grove OLED 128x96
  R11 = Resistor [tolerance=±5% resistance=220 package=THT]
  R12 = Resistor [tolerance=±5% resistance=220 package=THT]
  Key2_LED1 = LED - 3mm [color="Red (633nm)" package="3 mm [THT]"]
  R13 = Resistor [tolerance=±5% resistance=220 package=THT]
  Key2_LED2 = LED - 3mm [color="Red (633nm)" package="3 mm [THT]"]
  R14 = Resistor [tolerance=±5% resistance=220 package=THT]
  Key2_LED3 = LED - 3mm [color="Red (633nm)" package="3 mm [THT]"]
  R15 = Resistor [tolerance=±5% resistance=220 package=THT]
  Key2_LED4 = LED - 3mm [color="Red (633nm)" package="3 mm [THT]"]
  R16 = Resistor [tolerance=±5% resistance=220 package=THT]
  Key2_LED5 = LED - 3mm [color="Red (633nm)" package="3 mm [THT]"]
  R17 = Resistor [tolerance=±5% resistance=220 package=THT]
  Key2_LED6 = LED - 3mm [color="Red (633nm)" package="3 mm [THT]"]
  R18 = Resistor [tolerance=±5% resistance=220 package=THT]
  DC_to_DC_converter_12V_to_5V = RioRand LM2596
  U1 = LIPO-1000mAh [part_number=7.4V package=lipo-1000]  # not connected
  Key8 = Pushbutton [package="[THT]"]
  R8 = Resistor [tolerance=±5% resistance=3.3k package=THT]
  Battary_Charger = USB LiPoly Charger  # not connected

nets:
  N1: Part1.D1/TX, HC-1.RXD
  N2: Part1.D0/RX, HC-1.TXD
  GND: Part1.GND, HC-1.GND, Key1.Pin_1, Key1.Pin_2, Key2.Pin_1, Key2.Pin_2, Key3.Pin_1, Key3.Pin_2, Key4.Pin_1, Key4.Pin_2, Key5.Pin_1, Key5.Pin_2, Key6.Pin_1, Key6.Pin_2, Key7.Pin_1, Key7.Pin_2, R9.Pin_0, R10.Pin_1, R11.Pin_1, R12.Pin_1, R13.Pin_1, R14.Pin_1, R15.Pin_1, R16.Pin_1, R17.Pin_1, R18.Pin_1, DC_to_DC_converter_12V_to_5V.Pin_3, Key8.Pin_1, Key8.Pin_2
  N3: Part1.D2, Key1_LED.cathode
  N4: Part1.D3, Key2_LED.cathode
  N5: Part1.D4, Key2_LED1.cathode
  N6: Part1.D5, Key2_LED2.cathode
  N7: Part1.D6, Key2_LED3.cathode
  N8: Part1.D7, Key2_LED4.cathode
  N9: Part1.D8, Key2_LED5.cathode
  N10: Part1.D9, Key2_LED6.cathode
  N11: Part1.5V, R1.Pin_0
  N12: Part1.A7, R9.Pin_1
  N13: Part1.A5, Grove1.SCL
  N14: Part1.A4, Grove1.SDA
  N15: Part1.A3, Trim3.wiper
  N16: Part1.A2, Trim2.wiper
  N17: Part1.A1, Trim3_2.wiper
  N18: Part1.A0, R1.Pin_1, R2.Pin_0
  N19: Key2.Pin_3, Key2.Pin_4, R2.Pin_1, R3.Pin_0
  N20: Key3.Pin_3, R3.Pin_1, R4.Pin_0
  N21: Key4.Pin_3, R4.Pin_1, R5.Pin_1
  N22: Key5.Pin_3, R5.Pin_0, R6.Pin_0
  N23: Key6.Pin_3, R6.Pin_1, R7.Pin_0
  N24: Key7.Pin_3, Key7.Pin_4, R7.Pin_1, R8.Pin_0
  N25: Key8.Pin_3, R8.Pin_1

notes:
  5v

custom parts:
  HC-12 Module: HC-12 433Mhz Module
  HC-12 Antenna: Antenna for HC-12 433Mhz Module
