# Fritzing sketch Transmitter (saved by Fritzing 0.9.3b)

parts:
  Part1 = Arduino Nano (Rev3.0)
  HC-1 = HC-12 Module
  Antenna1 = HC-12 Antenna  # not connected
  Trim3 = Rotary Potentiometer (Large) [maximum_resistance=100kΩ package=THT]
  Trim2 = Rotary Potentiometer (Large) [maximum_resistance=100kΩ package=THT]
  Trim3_2 = Rotary Potentiometer (Large) [maximum_resistance=100kΩ package=THT]
  Key1_LED = LED - 3mm [color="Red (635nm)" package="3 mm [THT]"]
  Key2_LED = LED - 3mm [color="Red (633nm)" package="3 mm [THT]"]
  R10 = Resistor [tolerance=±5% resistance=5.1m package=THT]
  R11 = Resistor [tolerance=±5% resistance=10m package="0603 [SMD]"]
  C1 = Ceramic Capacitor [capacitance="100 nF" package="0805 [SMD, multilayer]"]  # not connected
  Grove1 = Grove OLED 128x96
  R12 = Resistor [tolerance=±5% resistance=220 package=THT]
  R13 = Resistor [tolerance=±5% resistance=220 package=THT]
  Key2_LED1 = LED - 3mm [color="Red (633nm)" package="3 mm [THT]"]
  R14 = Resistor [tolerance=±5% resistance=220 package=THT]
  Key2_LED2 = LED - 3mm [color="Red (633nm)" package="3 mm [THT]"]
  R15 = Resistor [tolerance=±5% resistance=220 package=THT]
  Key2_LED3 = LED - 3mm [color="Red (633nm)" package="3 mm [THT]"]
  R16 = Resistor [tolerance=±5% resistance=220 package=THT]
  Key2_LED4 = LED - 3mm [color="Red (633nm)" package="3 mm [THT]"]
  R17 = Resistor [tolerance=±5% resistance=220 package=THT]
  Key2_LED5 = LED - 3mm [color="Red (633nm)" package="3 mm [THT]"]
  R18 = Resistor [tolerance=±5% resistance=220 package=THT]
  Key2_LED6 = LED - 3mm [color="Red (633nm)" package="3 mm [THT]"]
  R19 = Resistor [tolerance=±5% resistance=220 package=THT]
  DC_to_DC_converter_12V_to_5V = RioRand LM2596
  U1 = LIPO-1000mAh [part_number=7.4V package=lipo-1000]  # not connected
  Battary_Charger = USB LiPoly Charger  # not connected
  R20 = Resistor [tolerance=±5% resistance=220 package=THT]
  Key2_LED7 = LED - 3mm [color="Red (633nm)" package="3 mm [THT]"]
  CD4048B1 = CD4048B [part_number=CD4048B package="DIP (Dual Inline) [THT]"]
  R21 = Resistor [tolerance=±5% resistance=10k package=THT]  # not connected
  Key1 = Pushbutton [package="[SMD]"]
  Key2 = Pushbutton [package="[SMD]"]
  Key3 = Pushbutton [package="[THT]"]
  Key13 = Pushbutton [package="[THT]"]
  Key14 = Pushbutton [package="[THT]"]
  Key15 = Pushbutton [package="[THT]"]
  Key16 = Pushbutton [package="[THT]"]
  Key17 = Pushbutton [package="[THT]"]
  Key18 = Pushbutton [package="[THT]"]
  R22 = Resistor [tolerance=±5% resistance=4.7k package=THT]
  R23 = Resistor [tolerance=±5% resistance=3.4k package=THT]
  R24 = Resistor [tolerance=±5% resistance=2.2k package=THT]
  R25 = Resistor [tolerance=±5% resistance=1.5k package=THT]
  R26 = Resistor [tolerance=±5% resistance=1k package=THT]
  R29 = Resistor [tolerance=±5% resistance=10k package=THT]  # not connected

nets:
  N1: Part1.D1/TX, HC-1.RXD
  N2: Part1.D0/RX, HC-1.TXD
  GND: Part1.GND, HC-1.GND, R12.Pin_1, R13.Pin_1, R14.Pin_1, R15.Pin_1, R16.Pin_1, R17.Pin_1, R18.Pin_1, R19.Pin_1, R20.Pin_1, CD4048B1.VSS
  N3: Part1.D5, Key1_LED.cathode
  N4: Part1.D6, Key2_LED.cathode
  N5: Part1.D7, Key2_LED1.cathode
  N6: Part1.D8, Key2_LED2.cathode
  N7: Part1.D9, Key2_LED3.cathode
  N8: Part1.D10, Key2_LED4.cathode
  N9: Part1.D11/MOSI, Key2_LED5.cathode
  N10: Part1.D12/MISO, Key2_LED6.cathode
  VCC: Part1.VIN, HC-1.VCC, Grove1.VCC, DC_to_DC_converter_12V_to_5V.Pin_2
  N11: Part1.A7, R10.Pin_1
  N12: Part1.A5, Grove1.SCL
  N13: Part1.A4, Grove1.SDA
  N14: Part1.A3, Trim3.wiper
  N15: Part1.A2, Trim2.wiper
  N16: Part1.A1, Trim3_2.wiper
  N17: Part1.D13/SCK, Key2_LED7.cathode
  N18: R10.Pin_0, R11.Pin_1, Grove1.GND, DC_to_DC_converter_12V_to_5V.Pin_3
  N19: CD4048B1.J, Key1.Pin_1, Key1.Pin_2
  N20: CD4048B1.EXPAND, Key2.Pin_2
  N21: Key3.Pin_1, Key3.Pin_2, Key13.Pin_1, Key13.Pin_2, Key14.Pin_1, Key14.Pin_2, Key15.Pin_1, Key15.Pin_2, Key16.Pin_1, Key16.Pin_2, Key17.Pin_1, Key17.Pin_2, Key18.Pin_1, Key18.Pin_2
  N22: Key14.Pin_3, R25.Pin_0, R26.Pin_0
  N23: Key15.Pin_3, R24.Pin_0, R25.Pin_1
  N24: Key16.Pin_3, R22.Pin_1
  N25: Key17.Pin_3, R22.Pin_0, R23.Pin_1
  N26: Key18.Pin_3, Key18.Pin_4, R23.Pin_0, R24.Pin_1

custom parts:
  HC-12 Module: HC-12 433Mhz Module
  HC-12 Antenna: Antenna for HC-12 433Mhz Module
